// Logisim project basicgates.circ as structural Verilog: 2 circuits, main circuit main
module main (
);

  wire adder1bit_1_output1, adder1bit_1_overflow;

  // Probe on adder1bit_1_overflow
  adder1bit adder1bit_1 (
    .inflow(1'b1), .input1(1'b1), .input2(1'b1), .overflow(adder1bit_1_overflow),
    .output1(adder1bit_1_output1));
  // Probe on adder1bit_1_output1
endmodule

module adder1bit (
  input  inflow,
  input  input1,
  input  input2,
  output overflow,
  output output1
);

  wire and_1_out, and_2_out, xor_1_out;

  and and_1 (and_1_out, input1, input2);
  xor xor_1 (xor_1_out, input1, input2);
  and and_2 (and_2_out, inflow, xor_1_out);
  xor xor_2 (output1, inflow, xor_1_out);
  or or_1 (overflow, and_1_out, and_2_out);
endmodule
